// Logisim project single_cycle_cpu.circ as structural Verilog
module main (
);

  wire and_1_out, button_1_out, button_2_out, button_3_out, button_4_out, button_6_out, counter_1_carry,
       counter_2_carry, rgb_video_1_p2;
  wire [4:0] counter_1_q, counter_2_q;

  cpu cpu_1 ();
  Button button_1 (.out(button_1_out));
  Button button_2 (.out(button_2_out));
  Button button_3 (.out(button_3_out));
  Button button_4 (.out(button_4_out));
  Button button_5 ();  // open: out
  Button button_6 (.out(button_6_out));
  Counter #(.max('h1f), .width(5)) counter_1 (
    .load(button_3_out), .count(button_2_out), .Q(counter_1_q), .carry(counter_1_carry), .up(1'b1),
    .clk(rgb_video_1_p2), .clr(button_6_out));  // open: D
  Counter #(.max('h1f), .width(5)) counter_2 (
    .load(button_1_out), .count(button_4_out), .Q(counter_2_q), .carry(counter_2_carry), .up(1'b1),
    .clk(rgb_video_1_p2), .clr(button_6_out));  // open: D
  and and_1 (and_1_out, counter_2_carry, counter_1_carry);
  // RGB_Video #(.height(32), .scale(6), .width(32)) rgb_video_1: pin names not known; wires that end beside it: and_1_out, rgb_video_1_p2, 1'b1, counter_1_q, counter_2_q, 24'hff0000
  Clock clock_1 (.out(rgb_video_1_p2));
endmodule

module interceptadorDeVideo (
  input  [9:0] Adress_in_29fa8d3b,
  input  Write_Enable_269089bd,
  input  [31:0] Data_in_a69cb09e,
  output [9:0] Adress_out_c5c8049c,
  output Write_memory_ae2d996e,
  output Write_video_23d02e86,
  output [31:0] Data_out_7d7247f8
);

  wire comparator_1_eq, comparator_1_gt, not_1_out;

  Comparator #(.width(10)) comparator_1 (
    .a(Adress_in_29fa8d3b), .b(10'h20), .gt(comparator_1_gt), .eq(comparator_1_eq), .lt(comparator_1_eq));
  not not_1 (not_1_out, comparator_1_gt);
  and and_1 (Write_memory_ae2d996e, Write_Enable_269089bd, comparator_1_gt);
  and and_2 (Write_video_23d02e86, not_1_out, Write_Enable_269089bd);

  assign Adress_out_c5c8049c = Adress_in_29fa8d3b;
  assign Data_out_7d7247f8 = Data_in_a69cb09e;

  // Notes on the sheet:
  //   mem video size
endmodule

module controladorDisplay (
  input  clock,
  input  write,
  input  [9:0] address,
  input  [31:0] data,
  output [31:0] saida_0_c2095f98,
  output [31:0] saida_1_1ce8aea1,
  output [31:0] saida_2_aeb6fde3,
  output [31:0] saida_3_30c0e4e9,
  output [31:0] saida_4_7c4512e4,
  output [31:0] saida_5_a13e1cd9,
  output [31:0] saida_6_f41071db,
  output [31:0] saida_7_e01e2922,
  output [31:0] saida_8_5287bfb6,
  output [31:0] saida_9_731c9c0e,
  output [31:0] saida_10_03538d52,
  output [31:0] saida_11_a19ba90f,
  output [31:0] saida_12_944b2be0,
  output [31:0] saida_13_ac07cda3,
  output [31:0] saida_14_8c52c00f,
  output [31:0] saida_15_1da1734d,
  output [31:0] saida_16_7957ee1f,
  output [31:0] saida_17_292dc726,
  output [31:0] saida_18_ee839943,
  output [31:0] saida_19_96d947d3,
  output [31:0] saida_20_271873f3,
  output [31:0] saida_21_1e354396,
  output [31:0] saida_22_216b2745,
  output [31:0] saida_23_a4ee78f7,
  output [31:0] saida_24_570d1f2b,
  output [31:0] saida_25_7a3475eb,
  output [31:0] saida_26_15ce5d6f,
  output [31:0] saida_27_36d1a187,
  output [31:0] saida_28_8ce25794,
  output [31:0] saida_29_86b65059,
  output [31:0] saida_30_7334f7e1,
  output [31:0] saida_31_7e4db262
);

  wire and_1_out, and_2_out, and_3_out, and_4_out, and_5_out, and_6_out, and_7_out, and_8_out, and_9_out,
       and_10_out, and_11_out, and_12_out, and_13_out, and_14_out, and_15_out, and_16_out, and_17_out,
       and_18_out, and_19_out, and_20_out, and_21_out, and_22_out, and_23_out, and_24_out, and_25_out,
       and_26_out, and_27_out, and_28_out, and_29_out, and_30_out, and_31_out, and_32_out, decoder_1_out0,
       decoder_1_out1, decoder_1_out2, decoder_1_out3, decoder_1_out4, decoder_1_out5, decoder_1_out6,
       decoder_1_out7, decoder_1_out8, decoder_1_out9, decoder_1_out10, decoder_1_out11, decoder_1_out12,
       decoder_1_out13, decoder_1_out14, decoder_1_out15, decoder_1_out16, decoder_1_out17, decoder_1_out18,
       decoder_1_out19, decoder_1_out20, decoder_1_out21, decoder_1_out22, decoder_1_out23, decoder_1_out24,
       decoder_1_out25, decoder_1_out26, decoder_1_out27, decoder_1_out28, decoder_1_out29, decoder_1_out30,
       decoder_1_out31;

  Decoder #(.select(5)) decoder_1 (
    .out0(decoder_1_out0), .out1(decoder_1_out1), .out2(decoder_1_out2), .out3(decoder_1_out3),
    .out4(decoder_1_out4), .out5(decoder_1_out5), .out6(decoder_1_out6), .out7(decoder_1_out7),
    .out8(decoder_1_out8), .out9(decoder_1_out9), .out10(decoder_1_out10), .out11(decoder_1_out11),
    .out12(decoder_1_out12), .out13(decoder_1_out13), .out14(decoder_1_out14), .out15(decoder_1_out15),
    .out16(decoder_1_out16), .out17(decoder_1_out17), .out18(decoder_1_out18), .out19(decoder_1_out19),
    .out20(decoder_1_out20), .out21(decoder_1_out21), .out22(decoder_1_out22), .out23(decoder_1_out23),
    .out24(decoder_1_out24), .out25(decoder_1_out25), .out26(decoder_1_out26), .out27(decoder_1_out27),
    .out28(decoder_1_out28), .out29(decoder_1_out29), .out30(decoder_1_out30), .out31(decoder_1_out31),
    .sel(address[4:0]));  // open: en
  and and_1 (and_1_out, write, decoder_1_out0);
  and and_2 (and_2_out, write, decoder_1_out1);
  and and_3 (and_3_out, write, decoder_1_out2);
  and and_4 (and_4_out, write, decoder_1_out3);
  and and_5 (and_5_out, write, decoder_1_out4);
  and and_6 (and_6_out, write, decoder_1_out5);
  and and_7 (and_7_out, write, decoder_1_out6);
  and and_8 (and_8_out, write, decoder_1_out7);
  and and_9 (and_9_out, write, decoder_1_out8);
  and and_10 (and_10_out, write, decoder_1_out9);
  and and_11 (and_11_out, write, decoder_1_out10);
  and and_12 (and_12_out, write, decoder_1_out11);
  and and_13 (and_13_out, write, decoder_1_out12);
  and and_14 (and_14_out, write, decoder_1_out13);
  and and_15 (and_15_out, write, decoder_1_out14);
  and and_16 (and_16_out, write, decoder_1_out15);
  and and_17 (and_17_out, write, decoder_1_out16);
  and and_18 (and_18_out, write, decoder_1_out17);
  and and_19 (and_19_out, write, decoder_1_out18);
  and and_20 (and_20_out, write, decoder_1_out19);
  and and_21 (and_21_out, write, decoder_1_out20);
  and and_22 (and_22_out, write, decoder_1_out21);
  and and_23 (and_23_out, write, decoder_1_out22);
  and and_24 (and_24_out, write, decoder_1_out23);
  and and_25 (and_25_out, write, decoder_1_out24);
  and and_26 (and_26_out, write, decoder_1_out25);
  and and_27 (and_27_out, write, decoder_1_out26);
  and and_28 (and_28_out, write, decoder_1_out27);
  and and_29 (and_29_out, write, decoder_1_out28);
  and and_30 (and_30_out, write, decoder_1_out29);
  and and_31 (and_31_out, write, decoder_1_out30);
  and and_32 (and_32_out, write, decoder_1_out31);
  Register #(.width(32)) register_1 (.D(data), .en(and_1_out), .Q(saida_0_c2095f98), .clk(clock));  // open: clr
  Register #(.width(32)) register_2 (.D(data), .en(and_2_out), .Q(saida_1_1ce8aea1), .clk(clock));  // open: clr
  Register #(.width(32)) register_3 (.D(data), .en(and_3_out), .Q(saida_2_aeb6fde3), .clk(clock));  // open: clr
  Register #(.width(32)) register_4 (.D(data), .en(and_4_out), .Q(saida_3_30c0e4e9), .clk(clock));  // open: clr
  Register #(.width(32)) register_5 (.D(data), .en(and_5_out), .Q(saida_4_7c4512e4), .clk(clock));  // open: clr
  Register #(.width(32)) register_6 (.D(data), .en(and_6_out), .Q(saida_5_a13e1cd9), .clk(clock));  // open: clr
  Register #(.width(32)) register_7 (.D(data), .en(and_7_out), .Q(saida_6_f41071db), .clk(clock));  // open: clr
  Register #(.width(32)) register_8 (.D(data), .en(and_8_out), .Q(saida_7_e01e2922), .clk(clock));  // open: clr
  Register #(.width(32)) register_9 (.D(data), .en(and_9_out), .Q(saida_8_5287bfb6), .clk(clock));  // open: clr
  Register #(.width(32)) register_10 (.D(data), .en(and_10_out), .Q(saida_9_731c9c0e), .clk(clock));  // open: clr
  Register #(.width(32)) register_11 (.D(data), .en(and_11_out), .Q(saida_10_03538d52), .clk(clock));  // open: clr
  Register #(.width(32)) register_12 (.D(data), .en(and_12_out), .Q(saida_11_a19ba90f), .clk(clock));  // open: clr
  Register #(.width(32)) register_13 (.D(data), .en(and_13_out), .Q(saida_12_944b2be0), .clk(clock));  // open: clr
  Register #(.width(32)) register_14 (.D(data), .en(and_14_out), .Q(saida_13_ac07cda3), .clk(clock));  // open: clr
  Register #(.width(32)) register_15 (.D(data), .en(and_15_out), .Q(saida_14_8c52c00f), .clk(clock));  // open: clr
  Register #(.width(32)) register_16 (.D(data), .en(and_16_out), .Q(saida_15_1da1734d), .clk(clock));  // open: clr
  Register #(.width(32)) register_17 (.D(data), .en(and_17_out), .Q(saida_16_7957ee1f), .clk(clock));  // open: clr
  Register #(.width(32)) register_18 (.D(data), .en(and_18_out), .Q(saida_17_292dc726), .clk(clock));  // open: clr
  Register #(.width(32)) register_19 (.D(data), .en(and_19_out), .Q(saida_18_ee839943), .clk(clock));  // open: clr
  Register #(.width(32)) register_20 (.D(data), .en(and_20_out), .Q(saida_19_96d947d3), .clk(clock));  // open: clr
  Register #(.width(32)) register_21 (.D(data), .en(and_21_out), .Q(saida_20_271873f3), .clk(clock));  // open: clr
  Register #(.width(32)) register_22 (.D(data), .en(and_22_out), .Q(saida_21_1e354396), .clk(clock));  // open: clr
  Register #(.width(32)) register_23 (.D(data), .en(and_23_out), .Q(saida_22_216b2745), .clk(clock));  // open: clr
  Register #(.width(32)) register_24 (.D(data), .en(and_24_out), .Q(saida_23_a4ee78f7), .clk(clock));  // open: clr
  Register #(.width(32)) register_25 (.D(data), .en(and_25_out), .Q(saida_24_570d1f2b), .clk(clock));  // open: clr
  Register #(.width(32)) register_26 (.D(data), .en(and_26_out), .Q(saida_25_7a3475eb), .clk(clock));  // open: clr
  Register #(.width(32)) register_27 (.D(data), .en(and_27_out), .Q(saida_26_15ce5d6f), .clk(clock));  // open: clr
  Register #(.width(32)) register_28 (.D(data), .en(and_28_out), .Q(saida_27_36d1a187), .clk(clock));  // open: clr
  Register #(.width(32)) register_29 (.D(data), .en(and_29_out), .Q(saida_28_8ce25794), .clk(clock));  // open: clr
  Register #(.width(32)) register_30 (.D(data), .en(and_30_out), .Q(saida_29_86b65059), .clk(clock));  // open: clr
  Register #(.width(32)) register_31 (.D(data), .en(and_31_out), .Q(saida_30_7334f7e1), .clk(clock));  // open: clr
  Register #(.width(32)) register_32 (.D(data), .en(and_32_out), .Q(saida_31_7e4db262), .clk(clock));  // open: clr

  // Notes on the sheet:
  //   saida_15_1da1734d: pull=down
endmodule

module cpu (
);

  wire ALUSrc, and_1_out, and_2_out, BneOrBeq, Branch, clk, clock_1_out, Equal, ExpBlock, ExpSrc0, ExpSrc1,
       ExpSrc2, ExRegWrite, Halt, HasExp, interceptadordevideo_1_write_memory_ae2d996e,
       interceptadordevideo_1_write_video_23d02e86, IsCOP0, IsEret, IsJAL, IsJR, IsShamt, IsSyscall, Jump,
       MemRead, MemtoReg, MemWrite, multiplexer_4_out, multiplexer_12_out, not_1_out, not_2_out, not_3_out,
       not_4_out, not_5_out, or_1_out, RegDst, RegWrite, statistics_1_p1, statistics_1_p2, statistics_1_p3,
       syscall_decoder_2f4aa45e_1_p2, xor_1_out, ZeroExtend;
  wire [3:0] ALUop, syscall_decoder_2f4aa45e_1_p7_2, syscall_decoder_2f4aa45e_1_p7_3,
       syscall_decoder_2f4aa45e_1_p7_4, syscall_decoder_2f4aa45e_1_p7_5;
  wire [4:0] multiplexer_6_out, multiplexer_7_out, multiplexer_8_out, multiplexer_9_out;
  wire [5:0] multiplexer_5_out;
  wire [8:0] demultiplexer_1_out0, demultiplexer_1_out1;
  wire [9:0] interceptadordevideo_1_adress_out_c5c8049c;
  wire [15:0] syscall_decoder_2f4aa45e_1_p7;
  wire [27:0] adder_1_out;
  wire [31:0] adder_2_out, adder_3_out, alu_1_p5, bit_extender_1_out, counter_1_q, counter_2_q, counter_3_q,
       cp0_1_dout, cp0_1_pcout, Cycle_q, immediate_extender_c02fde3f_1_p4, immediate_extender_c02fde3f_1_p8,
       interceptadordevideo_1_data_out_7d7247f8, multiplexer_1_out, multiplexer_3_out, multiplexer_10_out,
       multiplexer_11_out, multiplexer_13_out, multiplexer_14_out, multiplexer_15_out, multiplexer_16_out,
       multiplexer_17_out, multiplexer_18_out, multiplexer_19_out, PC_Buffer_3aac93db_q, PC_q, ram_1_dout,
       regfile_1_r1, rom_1_data, rom_2_data, shifter_1_out;
  wire [31:2] multiplexer_5_out_2;

  Multiplexer #(.width(32)) multiplexer_1 (
    .in0(multiplexer_18_out), .in1(cp0_1_pcout), .out(multiplexer_1_out), .sel(and_1_out));
  not not_1 (not_1_out, HasExp);
  and and_1 (and_1_out, IsEret, IsCOP0);
  Multiplexer multiplexer_2 (.in0(clock_1_out), .in1(1'b1), .out(clk), .sel(Halt));
  Clock clock_1 (.out(clock_1_out));
  Counter #(.max('hffffffff), .width(32)) Cycle (.Q(Cycle_q), .clk(clk));  // open: load, D, count, carry, up, clr
  Multiplexer #(.width(32)) multiplexer_3 (
    .in0(32'h800), .in1(multiplexer_1_out), .out(multiplexer_3_out), .sel(not_1_out));
  Multiplexer multiplexer_4 (.in0(clk), .in1(not_2_out), .out(multiplexer_4_out), .sel(or_1_out));
  or or_1 (or_1_out, HasExp, and_1_out);
  // Probe on Cycle_q
  Register #(.width(32)) PC (.D(multiplexer_3_out), .Q(PC_q), .clk(multiplexer_4_out));  // open: en, clr
  not not_2 (not_2_out, clk);
  Counter #(.max('hffffffff), .width(32)) counter_1 (
    .count(statistics_1_p3), .Q(counter_1_q), .clk(clk));  // open: load, D, carry, up, clr
  // Probe on counter_1_q
  ROM #(.addrWidth(9), .dataWidth(32)) rom_1 (.addr(demultiplexer_1_out0), .data(rom_1_data));
  Demultiplexer #(.width(9)) demultiplexer_1 (
    .out0(demultiplexer_1_out0), .out1(demultiplexer_1_out1), .in(PC_q[10:2]), .sel(PC_q[11]));
  ROM #(.addrWidth(9), .dataWidth(32)) rom_2 (.addr(demultiplexer_1_out1), .data(rom_2_data));
  Adder #(.width(32)) adder_1 (
    .a(32'h4), .b(PC_q), .out({multiplexer_5_out_2[31:28], adder_1_out}));  // open: cin, cout
  Counter #(.max('hffffffff), .width(32)) counter_2 (
    .count(statistics_1_p2), .Q(counter_2_q), .clk(clk));  // open: load, D, carry, up, clr
  // Probe on counter_2_q
  Register #(.width(32)) PC_Buffer_3aac93db (.D(PC_q), .Q(PC_Buffer_3aac93db_q), .clk(HasExp));  // open: en, clr
  Adder #(.width(32)) adder_2 (.a(PC_q), .b(32'h4), .out(adder_2_out));  // open: cin, cout
  Counter #(.max('hffffffff), .width(32)) counter_3 (
    .count(statistics_1_p1), .Q(counter_3_q), .clk(clk));  // open: load, D, carry, up, clr
  // Probe on counter_3_q
  // Statistics statistics_1: pin names not known; wires that end beside it: statistics_1_p1, statistics_1_p2, statistics_1_p3
  Multiplexer #(.width(32)) multiplexer_5 (
    .in0(rom_1_data), .in1(rom_2_data), .out({multiplexer_5_out, multiplexer_5_out_2[27:2]}), .sel(PC_q[11]));
  // Control control_1: pin names not known; wires that end beside it: multiplexer_5_out, multiplexer_5_out_2[7:2], IsJAL, RegWrite, MemtoReg, IsCOP0, MemWrite, MemRead, IsJR, Branch, BneOrBeq, Jump, ALUop, ALUSrc, IsShamt, IsSyscall
  Multiplexer #(.width(5)) multiplexer_6 (
    .in0(multiplexer_5_out_2[22:18]), .in1(multiplexer_5_out_2[17:13]), .out(multiplexer_6_out), .sel(RegDst));
  Multiplexer #(.width(5)) multiplexer_7 (
    .in0(multiplexer_6_out), .in1({5{1'b1}}), .out(multiplexer_7_out), .sel(IsJAL));
  CP0 cp0_1 (
    .clk(clk), .enable(IsCOP0), .Inst({multiplexer_5_out, multiplexer_5_out_2[27:2]}),
    .PCin(PC_Buffer_3aac93db_q), .Din(immediate_extender_c02fde3f_1_p4), .ExpSrc0(ExpSrc0),
    .ExpSrc1(ExpSrc1), .ExpSrc2(ExpSrc2), .PCout(cp0_1_pcout), .Dout(cp0_1_dout), .ExRegWrite(ExRegWrite),
    .ExpBlock(ExpBlock), .IsEret(IsEret), .HasExp(HasExp));
  Multiplexer #(.width(5)) multiplexer_8 (
    .in0(multiplexer_5_out_2[22:18]), .in1(5'b00100), .out(multiplexer_8_out), .sel(IsSyscall));
  // Immediate_Extender_c02fde3f immediate_extender_c02fde3f_1: pin names not known; wires that end beside it: multiplexer_5_out_2[12:8], RegDst, ZeroExtend, immediate_extender_c02fde3f_1_p4, cp0_1_dout, multiplexer_5_out_2[17:2], ZeroExtend, immediate_extender_c02fde3f_1_p8, 5'b00100
  Regfile regfile_1 (
    .RW(multiplexer_7_out), .Din(multiplexer_10_out), .WE(multiplexer_12_out), .clk(clk),
    .R1_2179165c(multiplexer_9_out), .R2_88a1ccfb(multiplexer_8_out), .R2(immediate_extender_c02fde3f_1_p4),
    .R1(regfile_1_r1));  // open: v0, a0
  Multiplexer #(.width(5)) multiplexer_9 (
    .in0(multiplexer_5_out_2[27:23]), .in1(5'b00010), .out(multiplexer_9_out), .sel(IsSyscall));
  Multiplexer #(.width(32)) multiplexer_10 (
    .in0(cp0_1_dout), .in1(multiplexer_11_out), .out(multiplexer_10_out), .sel(not_3_out));
  not not_3 (not_3_out, IsCOP0);
  Multiplexer #(.width(32)) multiplexer_11 (
    .in0(adder_2_out), .in1(multiplexer_19_out), .out(multiplexer_11_out), .sel(not_4_out));
  not not_4 (not_4_out, IsJAL);
  Multiplexer multiplexer_12 (
    .in0(RegWrite), .in1(ExRegWrite), .out(multiplexer_12_out), .sel(syscall_decoder_2f4aa45e_1_p2));
  // Syscall_Decoder_2f4aa45e syscall_decoder_2f4aa45e_1: pin names not known; wires that end beside it: IsCOP0, syscall_decoder_2f4aa45e_1_p2, regfile_1_r1, immediate_extender_c02fde3f_1_p4, clk, IsSyscall, {syscall_decoder_2f4aa45e_1_p7_5, syscall_decoder_2f4aa45e_1_p7_4, syscall_decoder_2f4aa45e_1_p7_3, syscall_decoder_2f4aa45e_1_p7_2, syscall_decoder_2f4aa45e_1_p7}, Halt
  Multiplexer #(.width(32)) multiplexer_13 (
    .in0(immediate_extender_c02fde3f_1_p4), .in1(immediate_extender_c02fde3f_1_p8), .out(multiplexer_13_out),
    .sel(ALUSrc));
  assign bit_extender_1_out = {{27{multiplexer_5_out_2[12]}}, multiplexer_5_out_2[12:8]};  // Bit_Extender bit_extender_1
  Shifter #(.width(32)) shifter_1 (.in(immediate_extender_c02fde3f_1_p8), .\dist (5'b00010), .out(shifter_1_out));
  xor xor_1 (xor_1_out, Equal, BneOrBeq);
  Multiplexer #(.width(32)) multiplexer_14 (
    .in0(regfile_1_r1), .in1(immediate_extender_c02fde3f_1_p4), .out(multiplexer_14_out), .sel(IsShamt));
  Multiplexer #(.width(32)) multiplexer_15 (
    .in0(multiplexer_13_out), .in1(bit_extender_1_out), .out(multiplexer_15_out), .sel(IsShamt));
  Adder #(.width(32)) adder_3 (
    .a({multiplexer_5_out_2[31:28], adder_1_out}), .b(shifter_1_out), .out(adder_3_out));  // open: cin, cout
  Hex_Digit_Display hex_digit_display_1 (.value(syscall_decoder_2f4aa45e_1_p7_5));  // open: dp
  Hex_Digit_Display hex_digit_display_2 (.value(syscall_decoder_2f4aa45e_1_p7_4));  // open: dp
  // ALU alu_1: pin names not known; wires that end beside it: multiplexer_14_out, multiplexer_15_out, Equal, ALUop, alu_1_p5
  and and_2 (and_2_out, Branch, xor_1_out);
  Hex_Digit_Display hex_digit_display_3 (.value(syscall_decoder_2f4aa45e_1_p7_3));  // open: dp
  Hex_Digit_Display hex_digit_display_4 (.value(syscall_decoder_2f4aa45e_1_p7_2));  // open: dp
  Button button_1 (.out(ExpSrc0));
  Multiplexer #(.width(32)) multiplexer_16 (
    .in0({multiplexer_5_out_2[31:28], adder_1_out}), .in1(adder_3_out), .out(multiplexer_16_out),
    .sel(and_2_out));
  not not_5 (not_5_out, Jump);
  Hex_Digit_Display hex_digit_display_5 (.value(syscall_decoder_2f4aa45e_1_p7[15:12]));  // open: dp
  Hex_Digit_Display hex_digit_display_6 (.value(syscall_decoder_2f4aa45e_1_p7[11:8]));  // open: dp
  Button button_2 (.out(ExpSrc1));
  Multiplexer #(.width(32)) multiplexer_17 (
    .in0({multiplexer_5_out_2, 2'b00}), .in1(multiplexer_16_out), .out(multiplexer_17_out), .sel(not_5_out));
  Hex_Digit_Display hex_digit_display_7 (.value(syscall_decoder_2f4aa45e_1_p7[7:4]));  // open: dp
  Hex_Digit_Display hex_digit_display_8 (.value(syscall_decoder_2f4aa45e_1_p7[3:0]));  // open: dp
  interceptadorDeVideo interceptadordevideo_1 (
    .Write_Enable_269089bd(MemWrite), .Data_in_a69cb09e(immediate_extender_c02fde3f_1_p4),
    .Adress_in_29fa8d3b(alu_1_p5[11:2]), .Data_out_7d7247f8(interceptadordevideo_1_data_out_7d7247f8),
    .Adress_out_c5c8049c(interceptadordevideo_1_adress_out_c5c8049c),
    .Write_memory_ae2d996e(interceptadordevideo_1_write_memory_ae2d996e),
    .Write_video_23d02e86(interceptadordevideo_1_write_video_23d02e86));
  Button button_3 (.out(ExpSrc2));
  Multiplexer #(.width(32)) multiplexer_18 (
    .in0(multiplexer_17_out), .in1(regfile_1_r1), .out(multiplexer_18_out), .sel(IsJR));
  RAM #(.addrWidth(10), .dataWidth(32)) ram_1 (
    .addr(interceptadordevideo_1_adress_out_c5c8049c), .we(interceptadordevideo_1_write_memory_ae2d996e),
    .oe(MemRead), .clk(clk), .din(interceptadordevideo_1_data_out_7d7247f8), .dout(ram_1_dout));
  controladorDisplay controladordisplay_1 (
    .data(interceptadordevideo_1_data_out_7d7247f8), .clock(clk),
    .write(interceptadordevideo_1_write_video_23d02e86), .address(interceptadordevideo_1_adress_out_c5c8049c));  // open: saida_8_5287bfb6, saida_9_731c9c0e, saida_10_03538d52, saida_11_a19ba90f, saida_12_944b2be0, saida_13_ac07cda3, saida_14_8c52c00f, saida_15_1da1734d, saida_16_7957ee1f, saida_17_292dc726, saida_18_ee839943, saida_19_96d947d3, saida_20_271873f3, saida_21_1e354396, saida_22_216b2745, saida_23_a4ee78f7, saida_24_570d1f2b, saida_25_7a3475eb, saida_26_15ce5d6f, saida_27_36d1a187, saida_28_8ce25794, saida_0_c2095f98, saida_29_86b65059, saida_30_7334f7e1, saida_31_7e4db262, saida_1_1ce8aea1, saida_2_aeb6fde3, saida_3_30c0e4e9, saida_4_7c4512e4, saida_5_a13e1cd9, saida_6_f41071db, saida_7_e01e2922
  Multiplexer #(.width(32)) multiplexer_19 (.in0(alu_1_p5), .in1(ram_1_dout), .out(multiplexer_19_out), .sel(MemtoReg));

  // Notes on the sheet:
  //   contents of rom_1 (hex, n*v repeats v):
  //   8c010004 8c210004 11042 ac220004 8c010004 8c010004 8c010004 8c210004 11042 ac220004 8c010004
  //   8c010004 8c010004 8c210004 11042 ac220004 8c010004 8c010004 8c010004 8c210004 11042 ac220004
  //   8c010004 8c010004 8c010004 8c210004 11042 ac220004 8c010004 8c010004 8c010004 8c210004 11042
  //   ac220004 8c010004 8c010004 8c010004 8c210004 11042 ac220004 8c010004 8c010004 8c010004 8c210004
  //   11042 ac220004 8c010004 8c010004 8c010004 8c210004 11042 ac220004 8c010004 8c010004 8c010004
  //   8c210004 11042 ac220004 8c010004 8c010004 8c010004 8c210004 11042 ac220004 8c010004 8c010004
  //   8c010004 8c210004 11042 ac220004 8c010004 8c010004 8c010004 8c210004 11042 ac220004 8c010004
  //   8c010004 8c010004 8c210004 11042 ac220004 8c010004 8c010004 8c010004 8c210004 11042 ac220004
  //   8c010004 8c010004 8c010004 8c210004 11042 ac220004 8c010004 8c010004 8c010004 8c210004 11042
  //   ac220004 8c010004 8c010004 8c010004 8c210004 11042 ac220004 8c010004 8c010004 8c010004 8c210004
  //   11042 ac220004 8c010004 8c010004 8c010004 8c210004 11042 ac220004 8c010004 8c010004 8c010004
  //   8c210004 11042 ac220004 8c010004 8c010004 8c010004 8c210004 11042 ac220004 8c010004 8c010004
  //   8c010004 8c210004 11042 ac220004 8c010004 8c010004 8c010004 8c210004 11042 ac220004 8c010004
  //   8c010004 8c010004 8c210004 11042 ac220004 8c010004 8c010004 8c010004 8c210004 11042 ac220004
  //   8c010004 8c010004 8c010004 8c210004 11042 ac220004 8c010004 8c010004
  //   Screen
endmodule
