// Logisim project pipeline.circ as structural Verilog: 4 circuits, main circuit IF_ID_feaac39b
// IF/ID
module IF_ID_feaac39b (
  input  clk,
  input  clr,
  input  [31:0] InstIF,
  input  [31:0] PCPlus4ID,
  input  En,
  output [31:0] InstID,
  output [31:0] PCPlus4IF
);

  Register #(.width(32)) register_1 (.D(InstIF), .en(En), .Q(InstID), .clk(clk), .clr(clr));
  Register #(.width(32)) register_2 (.D(PCPlus4ID), .en(En), .Q(PCPlus4IF), .clk(clk), .clr(clr));
endmodule

// ID/EX
module ID_EX_a948eaf0 (
  input  clk,
  input  clr,
  input  MemWriteID,
  input  [31:0] ImmID,
  input  [31:0] ShamtID,
  input  IsJALID,
  input  JumpID,
  input  IsShamtID,
  input  [31:0] R1ID,
  input  [31:0] in_10,
  input  BranchID,
  input  MemtoRegID,
  input  IsJRID,
  input  RegWriteID,
  input  [31:0] R2ID,
  input  [31:0] PCPlus4ID,
  input  IsSyscallID,
  input  BneOrBeqID,
  input  [3:0] ALUopID,
  input  ALUSrcID,
  input  [31:0] CP0Dout,
  input  [4:0] WriteReg_ID_78385b6d,
  input  IsExceptionID,
  input  MemReadID,
  input  in_25,
  input  En,
  output MemWriteEX,
  output [31:0] ImmEX,
  output [31:0] ShamtEX,
  output IsJALEX,
  output JumpEX,
  output IsShamtEX,
  output [31:0] R1EX,
  output [31:0] JumpAddr,
  output BranchEX,
  output MemtoRegEX,
  output IsJREX,
  output RegWriteEX,
  output [31:0] R2EX,
  output [31:0] PCPlusEX,
  output IsSyscallEX,
  output BneOrBeqEX,
  output [3:0] ALUopEX,
  output ALUSrcEX,
  output [31:0] out_45,
  output [4:0] WriteReg_EX_b87c6bca,
  output IsExceptionEX,
  output MemReadEX,
  output IsEret
);

  Register #(.width(32)) register_1 (.D(ImmID), .en(En), .Q(ImmEX), .clk(clk), .clr(clr));
  Register #(.width(32)) register_2 (.D(R1ID), .en(En), .Q(R1EX), .clk(clk), .clr(clr));
  Register #(.width(32)) register_3 (.D(R2ID), .en(En), .Q(R2EX), .clk(clk), .clr(clr));
  Register #(.width(32)) register_4 (.D(CP0Dout), .en(En), .Q(out_45), .clk(clk), .clr(clr));
  Register #(.width(32)) register_5 (.D(ShamtID), .en(En), .Q(ShamtEX), .clk(clk), .clr(clr));
  Register #(.width(32)) register_6 (.D(in_10), .en(En), .Q(JumpAddr), .clk(clk), .clr(clr));
  Register #(.width(32)) register_7 (.D(PCPlus4ID), .en(En), .Q(PCPlusEX), .clk(clk), .clr(clr));
  Register #(.width(1)) register_8 (.D(IsJALID), .en(En), .Q(IsJALEX), .clk(clk), .clr(clr));
  Register #(.width(1)) register_9 (.D(IsShamtID), .en(En), .Q(IsShamtEX), .clk(clk), .clr(clr));
  Register #(.width(1)) register_10 (.D(MemtoRegID), .en(En), .Q(MemtoRegEX), .clk(clk), .clr(clr));
  Register #(.width(1)) register_11 (.D(RegWriteID), .en(En), .Q(RegWriteEX), .clk(clk), .clr(clr));
  Register #(.width(1)) register_12 (.D(BneOrBeqID), .en(En), .Q(BneOrBeqEX), .clk(clk), .clr(clr));
  Register #(.width(1)) register_13 (.D(ALUSrcID), .en(En), .Q(ALUSrcEX), .clk(clk), .clr(clr));
  Register #(.width(1)) register_14 (.D(IsExceptionID), .en(En), .Q(IsExceptionEX), .clk(clk), .clr(clr));
  Register #(.width(1)) register_15 (.D(MemReadID), .en(En), .Q(MemReadEX), .clk(clk), .clr(clr));
  Register #(.width(1)) register_16 (.D(MemWriteID), .en(En), .Q(MemWriteEX), .clk(clk), .clr(clr));
  Register #(.width(1)) register_17 (.D(JumpID), .en(En), .Q(JumpEX), .clk(clk), .clr(clr));
  Register #(.width(1)) register_18 (.D(BranchID), .en(En), .Q(BranchEX), .clk(clk), .clr(clr));
  Register #(.width(1)) register_19 (.D(IsJRID), .en(En), .Q(IsJREX), .clk(clk), .clr(clr));
  Register #(.width(1)) register_20 (.D(IsSyscallID), .en(En), .Q(IsSyscallEX), .clk(clk), .clr(clr));
  Register #(.width(4)) register_21 (.D(ALUopID), .en(En), .Q(ALUopEX), .clk(clk), .clr(clr));
  Register #(.width(5)) register_22 (.D(WriteReg_ID_78385b6d), .en(En), .Q(WriteReg_EX_b87c6bca), .clk(clk), .clr(clr));
  Register #(.width(1)) register_23 (.D(in_25), .en(En), .Q(IsEret), .clk(clk), .clr(clr));
endmodule

// EX/MEM
module EX_MEM_a09b6ee1 (
  input  clk,
  input  clr,
  input  IsJALEX,
  input  [31:0] ALUResultEX,
  input  MemtoRegEX,
  input  RegWriteEX,
  input  [31:0] WriteDataEX,
  input  IsExceptionEX,
  input  [31:0] JumpAddrEX,
  input  MemReadEX,
  input  MemWriteEX,
  input  [31:0] CP0Dout,
  input  IsSyscallEX,
  input  [4:0] WriteReg_EX_b87c6bca,
  input  En,
  output IsJALMEM,
  output [31:0] ALUResultMEM,
  output MemtoRegMEM,
  output RegWriteMEM,
  output [31:0] WriteDataMEM,
  output IsExceptionMEM,
  output [31:0] JumpAddrMEM,
  output MemReadMEM,
  output MemWriteMEM,
  output [31:0] out_25,
  output IsSyscallMEM,
  output [4:0] WriteReg_MEM_5ebca91a
);

  Register #(.width(1)) register_1 (.D(IsJALEX), .en(En), .Q(IsJALMEM), .clk(clk), .clr(clr));
  Register #(.width(1)) register_2 (.D(MemtoRegEX), .en(En), .Q(MemtoRegMEM), .clk(clk), .clr(clr));
  Register #(.width(1)) register_3 (.D(RegWriteEX), .en(En), .Q(RegWriteMEM), .clk(clk), .clr(clr));
  Register #(.width(1)) register_4 (.D(IsExceptionEX), .en(En), .Q(IsExceptionMEM), .clk(clk), .clr(clr));
  Register #(.width(1)) register_5 (.D(MemReadEX), .en(En), .Q(MemReadMEM), .clk(clk), .clr(clr));
  Register #(.width(1)) register_6 (.D(MemWriteEX), .en(En), .Q(MemWriteMEM), .clk(clk), .clr(clr));
  Register #(.width(1)) register_7 (.D(IsSyscallEX), .en(En), .Q(IsSyscallMEM), .clk(clk), .clr(clr));
  Register #(.width(5)) register_8 (.D(WriteReg_EX_b87c6bca), .en(En), .Q(WriteReg_MEM_5ebca91a), .clk(clk), .clr(clr));
  Register #(.width(32)) register_9 (.D(ALUResultEX), .en(En), .Q(ALUResultMEM), .clk(clk), .clr(clr));
  Register #(.width(32)) register_10 (.D(WriteDataEX), .en(En), .Q(WriteDataMEM), .clk(clk), .clr(clr));
  Register #(.width(32)) register_11 (.D(JumpAddrEX), .en(En), .Q(JumpAddrMEM), .clk(clk), .clr(clr));
  Register #(.width(32)) register_12 (.D(CP0Dout), .en(En), .Q(out_25), .clk(clk), .clr(clr));
endmodule

// MEM/WBN
module MEM_WB_8edbe185 (
  input  clk,
  input  clr,
  input  IsJALMEM,
  input  [31:0] ALUResultMEM,
  input  MemtoRegMEM,
  input  RegWriteMEM,
  input  [31:0] ReadDataMEM,
  input  IsExceptionMEM,
  input  IsSyscallMEM,
  input  [31:0] JumpAddrMEM,
  input  [4:0] WriteReg_MEM_5ebca91a,
  input  [31:0] in_12,
  input  En,
  output IsJALWB,
  output [31:0] ALUResultWB,
  output MemtoRegWB,
  output RegWriteWB,
  output [31:0] ReadDataWB,
  output IsExceptionWB,
  output IsSyscallWB,
  output [31:0] JumpAddrWB,
  output [4:0] WriteReg_WB_311720f2,
  output [31:0] out_23
);

  Register #(.width(1)) register_1 (.D(IsJALMEM), .en(En), .Q(IsJALWB), .clk(clk), .clr(clr));
  Register #(.width(1)) register_2 (.D(MemtoRegMEM), .en(En), .Q(MemtoRegWB), .clk(clk), .clr(clr));
  Register #(.width(1)) register_3 (.D(RegWriteMEM), .en(En), .Q(RegWriteWB), .clk(clk), .clr(clr));
  Register #(.width(1)) register_4 (.D(IsExceptionMEM), .en(En), .Q(IsExceptionWB), .clk(clk), .clr(clr));
  Register #(.width(1)) register_5 (.D(IsSyscallMEM), .en(En), .Q(IsSyscallWB), .clk(clk), .clr(clr));
  Register #(.width(5)) register_6 (.D(WriteReg_MEM_5ebca91a), .en(En), .Q(WriteReg_WB_311720f2), .clk(clk), .clr(clr));
  Register #(.width(32)) register_7 (.D(ALUResultMEM), .en(En), .Q(ALUResultWB), .clk(clk), .clr(clr));
  Register #(.width(32)) register_8 (.D(ReadDataMEM), .en(En), .Q(ReadDataWB), .clk(clk), .clr(clr));
  Register #(.width(32)) register_9 (.D(JumpAddrMEM), .en(En), .Q(JumpAddrWB), .clk(clk), .clr(clr));
  Register #(.width(32)) register_10 (.D(in_12), .en(En), .Q(out_23), .clk(clk), .clr(clr));
endmodule
