// Logisim project regfile.circ as structural Verilog: 1 circuit, main circuit Regfile
module Regfile (
  input  [4:0] R1_2179165c,
  input  [4:0] R2_88a1ccfb,
  input  [4:0] RW,
  input  [31:0] Din,
  input  WE,
  input  clk,
  output [31:0] R1,
  output [31:0] a0,
  output [31:0] R2,
  output [31:0] v0
);

  wire demultiplexer_1_out0, demultiplexer_1_out1, demultiplexer_1_out2, demultiplexer_1_out3,
       demultiplexer_2_out0, demultiplexer_2_out1, demultiplexer_2_out2, demultiplexer_2_out3,
       demultiplexer_2_out4, demultiplexer_2_out5, demultiplexer_2_out6, demultiplexer_2_out7,
       demultiplexer_3_out0, demultiplexer_3_out1, demultiplexer_3_out2, demultiplexer_3_out3,
       demultiplexer_3_out4, demultiplexer_3_out5, demultiplexer_3_out6, demultiplexer_3_out7,
       demultiplexer_4_out0, demultiplexer_4_out1, demultiplexer_4_out2, demultiplexer_4_out3,
       demultiplexer_4_out4, demultiplexer_4_out5, demultiplexer_4_out6, demultiplexer_4_out7,
       demultiplexer_5_out0, demultiplexer_5_out1, demultiplexer_5_out2, demultiplexer_5_out3,
       demultiplexer_5_out4, demultiplexer_5_out5, demultiplexer_5_out6, demultiplexer_5_out7;
  wire [31:0] L_0_Zero_952f80c6_q, L_1_at_7d057dda_q, L_3_v1_2d3e9565_q, L_5_a1_d112eca5_q,
       L_6_a2_8aec3816_q, L_7_a3_82656c4d_q, L_8_t0_42c87689_q, L_9_t1_edc7cf33_q, L_10_t2_e7de443e_q,
       L_11_t3_f55c5ac1_q, L_12_t4_8ba781f7_q, L_13_t5_70b81709_q, L_14_t6_43d03d95_q, L_15_t7_78cd901f_q,
       L_19_s3_917c8ae3_q, L_20_s4_65e0948d_q, L_21_s5_771ae8d6_q, L_22_s6_c2ffc309_q, L_23_s7_596232de_q,
       L_24_t8_578d3dac_q, L_25_t9_2ca3739c_q, L_26_k0_6975dac2_q, L_27_k1_7996bc01_q, L_28_gp_85b57eb7_q,
       L_29_sp_d61e2c7c_q, L_30_fp_026454e2_q, L_ra_1389d1af, L_s0_5ef24bd4, L_s1_044d4850, L_s2_6ad457ec;

  Demultiplexer #(.enable("true"), .select(2)) demultiplexer_1 (
    .out0(demultiplexer_1_out0), .out1(demultiplexer_1_out1), .out2(demultiplexer_1_out2),
    .out3(demultiplexer_1_out3), .in(1'b1), .sel(RW[4:3]), .en(WE));
  Demultiplexer #(.enable("true"), .select(3)) demultiplexer_2 (
    .out0(demultiplexer_2_out0), .out1(demultiplexer_2_out1), .out2(demultiplexer_2_out2),
    .out3(demultiplexer_2_out3), .out4(demultiplexer_2_out4), .out5(demultiplexer_2_out5),
    .out6(demultiplexer_2_out6), .out7(demultiplexer_2_out7), .in(1'b1), .sel(RW[2:0]),
    .en(demultiplexer_1_out0));
  Demultiplexer #(.enable("true"), .select(3)) demultiplexer_3 (
    .out0(demultiplexer_3_out0), .out1(demultiplexer_3_out1), .out2(demultiplexer_3_out2),
    .out3(demultiplexer_3_out3), .out4(demultiplexer_3_out4), .out5(demultiplexer_3_out5),
    .out6(demultiplexer_3_out6), .out7(demultiplexer_3_out7), .in(1'b1), .sel(RW[2:0]),
    .en(demultiplexer_1_out1));
  Demultiplexer #(.enable("true"), .select(3)) demultiplexer_4 (
    .out0(demultiplexer_4_out0), .out1(demultiplexer_4_out1), .out2(demultiplexer_4_out2),
    .out3(demultiplexer_4_out3), .out4(demultiplexer_4_out4), .out5(demultiplexer_4_out5),
    .out6(demultiplexer_4_out6), .out7(demultiplexer_4_out7), .in(1'b1), .sel(RW[2:0]),
    .en(demultiplexer_1_out2));
  Demultiplexer #(.enable("true"), .select(3)) demultiplexer_5 (
    .out0(demultiplexer_5_out0), .out1(demultiplexer_5_out1), .out2(demultiplexer_5_out2),
    .out3(demultiplexer_5_out3), .out4(demultiplexer_5_out4), .out5(demultiplexer_5_out5),
    .out6(demultiplexer_5_out6), .out7(demultiplexer_5_out7), .in(1'b1), .sel(RW[2:0]),
    .en(demultiplexer_1_out3));
  Register #(.width(32)) L_0_Zero_952f80c6 (
    .D(Din), .en(demultiplexer_2_out0), .Q(L_0_Zero_952f80c6_q));  // open: clk, clr
  Register #(.width(32)) L_8_t0_42c87689 (
    .D(Din), .en(demultiplexer_3_out0), .Q(L_8_t0_42c87689_q), .clk(clk));  // open: clr
  Register #(.width(32)) L_16_s0_7c9a8e2b (
    .D(Din), .en(demultiplexer_4_out0), .Q(L_s0_5ef24bd4), .clk(clk));  // open: clr
  Register #(.width(32)) L_24_t8_578d3dac (
    .D(Din), .en(demultiplexer_5_out0), .Q(L_24_t8_578d3dac_q), .clk(clk));  // open: clr
  Register #(.width(32)) L_1_at_7d057dda (
    .D(Din), .en(demultiplexer_2_out1), .Q(L_1_at_7d057dda_q), .clk(clk));  // open: clr
  Register #(.width(32)) L_9_t1_edc7cf33 (
    .D(Din), .en(demultiplexer_3_out1), .Q(L_9_t1_edc7cf33_q), .clk(clk));  // open: clr
  Register #(.width(32)) L_17_s1_edfea873 (
    .D(Din), .en(demultiplexer_4_out1), .Q(L_s1_044d4850), .clk(clk));  // open: clr
  Register #(.width(32)) L_25_t9_2ca3739c (
    .D(Din), .en(demultiplexer_5_out1), .Q(L_25_t9_2ca3739c_q), .clk(clk));  // open: clr
  Register #(.width(32)) L_2_v0_f02eb05a (.D(Din), .en(demultiplexer_2_out2), .Q(v0), .clk(clk));  // open: clr
  Register #(.width(32)) L_10_t2_e7de443e (
    .D(Din), .en(demultiplexer_3_out2), .Q(L_10_t2_e7de443e_q), .clk(clk));  // open: clr
  Register #(.width(32)) L_18_s2_e291283e (
    .D(Din), .en(demultiplexer_4_out2), .Q(L_s2_6ad457ec), .clk(clk));  // open: clr
  Register #(.width(32)) L_26_k0_6975dac2 (
    .D(Din), .en(demultiplexer_5_out2), .Q(L_26_k0_6975dac2_q), .clk(clk));  // open: clr
  Register #(.width(32)) L_3_v1_2d3e9565 (
    .D(Din), .en(demultiplexer_2_out3), .Q(L_3_v1_2d3e9565_q), .clk(clk));  // open: clr
  Register #(.width(32)) L_11_t3_f55c5ac1 (
    .D(Din), .en(demultiplexer_3_out3), .Q(L_11_t3_f55c5ac1_q), .clk(clk));  // open: clr
  Register #(.width(32)) L_19_s3_917c8ae3 (
    .D(Din), .en(demultiplexer_4_out3), .Q(L_19_s3_917c8ae3_q), .clk(clk));  // open: clr
  Register #(.width(32)) L_27_k1_7996bc01 (
    .D(Din), .en(demultiplexer_5_out3), .Q(L_27_k1_7996bc01_q), .clk(clk));  // open: clr
  Register #(.width(32)) L_4_a0_4aee8dc9 (.D(Din), .en(demultiplexer_2_out4), .Q(a0), .clk(clk));  // open: clr
  Register #(.width(32)) L_12_t4_8ba781f7 (
    .D(Din), .en(demultiplexer_3_out4), .Q(L_12_t4_8ba781f7_q), .clk(clk));  // open: clr
  Register #(.width(32)) L_20_s4_65e0948d (
    .D(Din), .en(demultiplexer_4_out4), .Q(L_20_s4_65e0948d_q), .clk(clk));  // open: clr
  Register #(.width(32)) L_28_gp_85b57eb7 (
    .D(Din), .en(demultiplexer_5_out4), .Q(L_28_gp_85b57eb7_q), .clk(clk));  // open: clr
  Register #(.width(32)) L_5_a1_d112eca5 (
    .D(Din), .en(demultiplexer_2_out5), .Q(L_5_a1_d112eca5_q), .clk(clk));  // open: clr
  Register #(.width(32)) L_13_t5_70b81709 (
    .D(Din), .en(demultiplexer_3_out5), .Q(L_13_t5_70b81709_q), .clk(clk));  // open: clr
  Register #(.width(32)) L_21_s5_771ae8d6 (
    .D(Din), .en(demultiplexer_4_out5), .Q(L_21_s5_771ae8d6_q), .clk(clk));  // open: clr
  Register #(.width(32)) L_29_sp_d61e2c7c (
    .D(Din), .en(demultiplexer_5_out5), .Q(L_29_sp_d61e2c7c_q), .clk(clk));  // open: clr
  Register #(.width(32)) L_6_a2_8aec3816 (
    .D(Din), .en(demultiplexer_2_out6), .Q(L_6_a2_8aec3816_q), .clk(clk));  // open: clr
  Register #(.width(32)) L_14_t6_43d03d95 (
    .D(Din), .en(demultiplexer_3_out6), .Q(L_14_t6_43d03d95_q), .clk(clk));  // open: clr
  Register #(.width(32)) L_22_s6_c2ffc309 (
    .D(Din), .en(demultiplexer_4_out6), .Q(L_22_s6_c2ffc309_q), .clk(clk));  // open: clr
  Register #(.width(32)) L_30_fp_026454e2 (
    .D(Din), .en(demultiplexer_5_out6), .Q(L_30_fp_026454e2_q), .clk(clk));  // open: clr
  Register #(.width(32)) L_7_a3_82656c4d (
    .D(Din), .en(demultiplexer_2_out7), .Q(L_7_a3_82656c4d_q), .clk(clk));  // open: clr
  Register #(.width(32)) L_15_t7_78cd901f (
    .D(Din), .en(demultiplexer_3_out7), .Q(L_15_t7_78cd901f_q), .clk(clk));  // open: clr
  Register #(.width(32)) L_23_s7_596232de (
    .D(Din), .en(demultiplexer_4_out7), .Q(L_23_s7_596232de_q), .clk(clk));  // open: clr
  Register #(.width(32)) L_31_ra_05260f4d (
    .D(Din), .en(demultiplexer_5_out7), .Q(L_ra_1389d1af), .clk(clk));  // open: clr
  Multiplexer #(.select(5), .width(32)) multiplexer_1 (
    .in0(L_0_Zero_952f80c6_q), .in1(L_1_at_7d057dda_q), .in2(v0), .in3(L_3_v1_2d3e9565_q), .in4(a0),
    .in5(L_5_a1_d112eca5_q), .in6(L_6_a2_8aec3816_q), .in7(L_7_a3_82656c4d_q), .in8(L_8_t0_42c87689_q),
    .in9(L_9_t1_edc7cf33_q), .in10(L_10_t2_e7de443e_q), .in11(L_11_t3_f55c5ac1_q), .in12(L_12_t4_8ba781f7_q),
    .in13(L_13_t5_70b81709_q), .in14(L_14_t6_43d03d95_q), .in15(L_15_t7_78cd901f_q), .in16(L_s0_5ef24bd4),
    .in17(L_s1_044d4850), .in18(L_s2_6ad457ec), .in19(L_19_s3_917c8ae3_q), .in20(L_20_s4_65e0948d_q),
    .in21(L_21_s5_771ae8d6_q), .in22(L_22_s6_c2ffc309_q), .in23(L_23_s7_596232de_q),
    .in24(L_24_t8_578d3dac_q), .in25(L_25_t9_2ca3739c_q), .in26(L_26_k0_6975dac2_q),
    .in27(L_27_k1_7996bc01_q), .in28(L_28_gp_85b57eb7_q), .in29(L_29_sp_d61e2c7c_q),
    .in30(L_30_fp_026454e2_q), .in31(L_ra_1389d1af), .out(R1), .sel(R1_2179165c));
  Multiplexer #(.select(5), .width(32)) multiplexer_2 (
    .in0(L_0_Zero_952f80c6_q), .in1(L_1_at_7d057dda_q), .in2(v0), .in3(L_3_v1_2d3e9565_q), .in4(a0),
    .in5(L_5_a1_d112eca5_q), .in6(L_6_a2_8aec3816_q), .in7(L_7_a3_82656c4d_q), .in8(L_8_t0_42c87689_q),
    .in9(L_9_t1_edc7cf33_q), .in10(L_10_t2_e7de443e_q), .in11(L_11_t3_f55c5ac1_q), .in12(L_12_t4_8ba781f7_q),
    .in13(L_13_t5_70b81709_q), .in14(L_14_t6_43d03d95_q), .in15(L_15_t7_78cd901f_q), .in16(L_s0_5ef24bd4),
    .in17(L_s1_044d4850), .in18(L_s2_6ad457ec), .in19(L_19_s3_917c8ae3_q), .in20(L_20_s4_65e0948d_q),
    .in21(L_21_s5_771ae8d6_q), .in22(L_22_s6_c2ffc309_q), .in23(L_23_s7_596232de_q),
    .in24(L_24_t8_578d3dac_q), .in25(L_25_t9_2ca3739c_q), .in26(L_26_k0_6975dac2_q),
    .in27(L_27_k1_7996bc01_q), .in28(L_28_gp_85b57eb7_q), .in29(L_29_sp_d61e2c7c_q),
    .in30(L_30_fp_026454e2_q), .in31(L_ra_1389d1af), .out(R2), .sel(R2_88a1ccfb));

  // Other names for the same wires on the sheet: L_a0_cef34b9f[31:0] = a0; L_v0_2632fe78[31:0] = v0; reg1[31:0] = R1;
  //   reg1_ccfc47f3[4:0] = R1_2179165c; reg2[31:0] = R2; reg2_cc07ae4f[4:0] = R2_88a1ccfb; write_data[31:0] = Din;
  //   write_reg_62490d23[4:0] = RW

  // Notes on the sheet:
  //   Input
  //   Output
endmodule
