// Logisim project single_cycle_cpu.circ as structural Verilog
module main (
);

  wire and_1_out, button_1_out, button_2_out, button_3_out, button_4_out, button_6_out, counter_1_carry,
       counter_2_carry, rgb_video_1_p2;
  wire [4:0] counter_1_q, counter_2_q;

  Button button_1 (.out(button_1_out));
  Button button_2 (.out(button_2_out));
  Button button_3 (.out(button_3_out));
  Button button_4 (.out(button_4_out));
  Button button_5 ();  // open: out
  Button button_6 (.out(button_6_out));
  Counter #(.max('h1f), .width(5)) counter_1 (
    .load(button_3_out), .count(button_2_out), .Q(counter_1_q), .carry(counter_1_carry), .up(1'b1),
    .clk(rgb_video_1_p2), .clr(button_6_out));  // open: D
  cpu cpu_1 ();  // open: Reset, Clock, clear_video, out_4, out_5, out_6, out_7
  Counter #(.max('h1f), .width(5)) counter_2 (
    .load(button_1_out), .count(button_4_out), .Q(counter_2_q), .carry(counter_2_carry), .up(1'b1),
    .clk(rgb_video_1_p2), .clr(button_6_out));  // open: D
  and and_1 (and_1_out, counter_2_carry, counter_1_carry);
  // RGB_Video #(.height(32), .scale(6), .width(32)) rgb_video_1: pin names not known; wires that end beside it: and_1_out, rgb_video_1_p2, 1'b1, counter_1_q, counter_2_q, 24'hff0000
  Clock clock_1 (.out(rgb_video_1_p2));
endmodule

module interceptadorDeVideo (
  input  [31:0] Data_in,
  input  [9:0] Adress_in,
  input  Write_Enable,
  input  in_4,
  output [31:0] Data_out,
  output [9:0] Adress_out,
  output Write_memory,
  output enable_video
);

  wire comparator_1_eq, comparator_1_gt, comparator_2_eq, comparator_2_lt, not_1_out, or_1_out, or_2_out;
  wire [9:0] adder_1_out;

  Adder #(.width(10)) adder_1 (.a(10'h20), .b(10'h20), .out(adder_1_out), .cin(in_4));  // open: cout
  Comparator #(.width(10)) comparator_1 (
    .a(Adress_in), .b(10'h20), .gt(comparator_1_gt), .eq(comparator_1_eq));  // open: lt
  Comparator #(.width(10)) comparator_2 (
    .a(Adress_in), .b(adder_1_out), .eq(comparator_2_eq), .lt(comparator_2_lt));  // open: gt
  or or_1 (or_1_out, comparator_1_gt, comparator_1_eq);
  or or_2 (or_2_out, comparator_2_eq, comparator_2_lt);
  not not_1 (not_1_out, enable_video);
  and and_1 (enable_video, or_1_out, or_2_out);
  and and_2 (Write_memory, Write_Enable, not_1_out);

  assign Adress_out = Adress_in;
  assign Data_out = Data_in;

  // Notes on the sheet:
  //   mem video at
  //   mem video size
endmodule

module controladorDisplay (
  input  clock,
  input  enable,
  input  clear,
  input  [9:0] address,
  input  [31:0] data,
  output [31:0] data_out,
  output [4:0] X,
  output [4:0] y,
  output [23:0] color
);

  wire comparator_1_eq, comparator_2_eq, comparator_3_eq;
  wire [4:0] and_1_out, and_2_out, bit_extender_1_out, bit_extender_2_out, bitselector_2_out,
       bitselector_3_out;
  wire [23:0] and_3_out, bit_extender_3_out, bitselector_1_out;

  Comparator #(.width(10)) comparator_1 (.a(address), .b(10'h20), .eq(comparator_1_eq));  // open: gt, lt
  Comparator #(.width(10)) comparator_2 (.a(address), .b(10'h21), .eq(comparator_2_eq));  // open: gt, lt
  Comparator #(.width(10)) comparator_3 (.a(address), .b(10'h22), .eq(comparator_3_eq));  // open: gt, lt
  BitSelector #(.group(24), .width(32)) bitselector_1 (.in(data), .out(bitselector_1_out), .sel(1'b0));
  BitSelector #(.group(5), .width(32)) bitselector_2 (.in(data), .out(bitselector_2_out), .sel(3'b000));
  BitSelector #(.group(5), .width(32)) bitselector_3 (.in(data), .out(bitselector_3_out), .sel(3'b000));
  assign bit_extender_1_out = {{4{comparator_1_eq}}, comparator_1_eq};  // Bit_Extender bit_extender_1
  assign bit_extender_2_out = {{4{comparator_2_eq}}, comparator_2_eq};  // Bit_Extender bit_extender_2
  assign bit_extender_3_out = {{23{comparator_3_eq}}, comparator_3_eq};  // Bit_Extender bit_extender_3
  assign and_1_out = bitselector_3_out & bit_extender_1_out;  // AND_Gate and_1, 5 bits wide
  assign and_2_out = bitselector_2_out & bit_extender_2_out;  // AND_Gate and_2, 5 bits wide
  assign and_3_out = bitselector_1_out & bit_extender_3_out;  // AND_Gate and_3, 24 bits wide
  Register #(.width(5)) register_1 (.D(and_1_out), .en(enable), .Q(X), .clk(clock), .clr(clear));
  Register #(.width(5)) register_2 (.D(and_2_out), .en(enable), .Q(y), .clk(clock), .clr(clear));
  Register #(.width(24)) register_3 (.D(and_3_out), .en(enable), .Q(color), .clk(clock), .clr(clear));

  assign data_out = data;
endmodule

module cpu (
  input  Reset,
  input  Clock,
  input  clear_video,
  output [4:0] out_4,
  output [4:0] out_5,
  output [23:0] out_6,
  output [31:0] out_7
);

  wire ALUSrc, and_1_out, and_2_out, BneOrBeq, Branch, clk, Equal, ExpBlock, ExpSrc0, ExpSrc1, ExpSrc2,
       ExRegWrite, Halt, HasExp, interceptadordevideo_1_enable_video, interceptadordevideo_1_write_memory,
       IsCOP0, IsEret, IsJAL, IsJR, IsShamt, IsSyscall, Jump, MemRead, MemtoReg, MemWrite, multiplexer_4_out,
       multiplexer_12_out, not_1_out, not_2_out, not_3_out, not_4_out, not_5_out, or_1_out, RegDst, RegWrite,
       statistics_1_p1, statistics_1_p2, statistics_1_p3, undriven, xor_1_out, ZeroExtend;
  wire [3:0] ALUop, syscall_decoder_7b4aca82_1_hex_2, syscall_decoder_7b4aca82_1_hex_3,
       syscall_decoder_7b4aca82_1_hex_4, syscall_decoder_7b4aca82_1_hex_5;
  wire [4:0] multiplexer_6_out, multiplexer_7_out, multiplexer_8_out, multiplexer_9_out;
  wire [5:0] multiplexer_5_out;
  wire [8:0] demultiplexer_1_out0, demultiplexer_1_out1;
  wire [9:0] interceptadordevideo_1_adress_out;
  wire [15:0] syscall_decoder_7b4aca82_1_hex;
  wire [27:0] adder_1_out;
  wire [31:0] adder_2_out, adder_3_out, alu_1_p5, bit_extender_1_out, counter_1_q, counter_2_q, counter_3_q,
       cp0_1_dout, cp0_1_pcout, Cycle_q, immediate_extender_0b85654b_1_output,
       interceptadordevideo_1_data_out, multiplexer_1_out, multiplexer_3_out, multiplexer_10_out,
       multiplexer_11_out, multiplexer_13_out, multiplexer_14_out, multiplexer_15_out, multiplexer_16_out,
       multiplexer_17_out, multiplexer_18_out, multiplexer_19_out, PC_Buffer_3aac93db_q, PC_q, ram_1_dout,
       regfile_1_r1, regfile_1_r2, rom_1_data, rom_2_data, shifter_1_out;
  wire [31:2] multiplexer_5_out_2;

  Multiplexer #(.width(32)) multiplexer_1 (
    .in0(multiplexer_18_out), .in1(cp0_1_pcout), .out(multiplexer_1_out), .sel(and_1_out));
  not not_1 (not_1_out, HasExp);
  and and_1 (and_1_out, IsEret, IsCOP0);
  Multiplexer multiplexer_2 (.in0(Clock), .in1(1'b1), .out(clk), .sel(Halt));
  Counter #(.max('hffffffff), .width(32)) Cycle (.Q(Cycle_q), .clk(clk));  // open: load, D, count, carry, up, clr
  Multiplexer #(.width(32)) multiplexer_3 (
    .in0(32'h800), .in1(multiplexer_1_out), .out(multiplexer_3_out), .sel(not_1_out));
  Multiplexer multiplexer_4 (.in0(clk), .in1(not_2_out), .out(multiplexer_4_out), .sel(or_1_out));
  or or_1 (or_1_out, HasExp, and_1_out);
  // Probe on Cycle_q
  Register #(.width(32)) PC (.D(multiplexer_3_out), .Q(PC_q), .clk(multiplexer_4_out), .clr(Reset));  // open: en
  not not_2 (not_2_out, clk);
  Counter #(.max('hffffffff), .width(32)) counter_1 (
    .count(statistics_1_p3), .Q(counter_1_q), .clk(clk));  // open: load, D, carry, up, clr
  // Probe on counter_1_q
  ROM #(.addrWidth(9), .dataWidth(32)) rom_1 (.addr(demultiplexer_1_out0), .data(rom_1_data));
  Demultiplexer #(.width(9)) demultiplexer_1 (
    .out0(demultiplexer_1_out0), .out1(demultiplexer_1_out1), .in(PC_q[10:2]), .sel(PC_q[11]));
  ROM #(.addrWidth(9), .dataWidth(32)) rom_2 (.addr(demultiplexer_1_out1), .data(rom_2_data));
  Adder #(.width(32)) adder_1 (
    .a(32'h4), .b(PC_q), .out({multiplexer_5_out_2[31:28], adder_1_out}));  // open: cin, cout
  Counter #(.max('hffffffff), .width(32)) counter_2 (
    .count(statistics_1_p2), .Q(counter_2_q), .clk(clk));  // open: load, D, carry, up, clr
  // Probe on counter_2_q
  Register #(.width(32)) PC_Buffer_3aac93db (.D(PC_q), .Q(PC_Buffer_3aac93db_q), .clk(HasExp));  // open: en, clr
  Adder #(.width(32)) adder_2 (.a(PC_q), .b(32'h4), .out(adder_2_out));  // open: cin, cout
  Counter #(.max('hffffffff), .width(32)) counter_3 (
    .count(statistics_1_p1), .Q(counter_3_q), .clk(clk));  // open: load, D, carry, up, clr
  // Probe on counter_3_q
  // Statistics statistics_1: pin names not known; wires that end beside it: statistics_1_p1, statistics_1_p2, statistics_1_p3
  Multiplexer #(.width(32)) multiplexer_5 (
    .in0(rom_1_data), .in1(rom_2_data), .out({multiplexer_5_out, multiplexer_5_out_2[27:2]}), .sel(PC_q[11]));
  // Control control_1: pin names not known; wires that end beside it: multiplexer_5_out, multiplexer_5_out_2[7:2], IsJAL, RegWrite, MemtoReg, IsCOP0, MemWrite, MemRead, IsJR, Branch, BneOrBeq, Jump, ALUop, ALUSrc, IsShamt, IsSyscall, RegDst, ZeroExtend
  Multiplexer #(.width(5)) multiplexer_6 (
    .in0(multiplexer_5_out_2[22:18]), .in1(multiplexer_5_out_2[17:13]), .out(multiplexer_6_out), .sel(RegDst));
  Multiplexer #(.width(5)) multiplexer_7 (
    .in0(multiplexer_6_out), .in1({5{1'b1}}), .out(multiplexer_7_out), .sel(IsJAL));
  CP0 cp0_1 (
    .clk(clk), .enable(IsCOP0), .Inst({multiplexer_5_out, multiplexer_5_out_2[27:2]}),
    .PCin(PC_Buffer_3aac93db_q), .Din(regfile_1_r2), .ExpSrc0(ExpSrc0), .ExpSrc1(ExpSrc1), .ExpSrc2(ExpSrc2),
    .PCout(cp0_1_pcout), .Dout(cp0_1_dout), .ExRegWrite(ExRegWrite), .ExpBlock(ExpBlock), .IsEret(IsEret),
    .HasExp(HasExp));
  Multiplexer #(.width(5)) multiplexer_8 (
    .in0(multiplexer_5_out_2[22:18]), .in1(5'b00100), .out(multiplexer_8_out), .sel(IsSyscall));
  Immediate_Extender_0b85654b immediate_extender_0b85654b_1 (
    .Input(multiplexer_5_out_2[17:2]), .ZeroExtend(ZeroExtend), .Output(immediate_extender_0b85654b_1_output));
  Regfile regfile_1 (
    .RW(multiplexer_7_out), .Din(multiplexer_10_out), .WE(multiplexer_12_out), .clk(clk),
    .R1_2179165c(multiplexer_9_out), .R2_88a1ccfb(multiplexer_8_out), .R2(regfile_1_r2), .R1(regfile_1_r1));  // open: v0, a0
  Multiplexer #(.width(5)) multiplexer_9 (
    .in0(multiplexer_5_out_2[27:23]), .in1(5'b00010), .out(multiplexer_9_out), .sel(IsSyscall));
  Multiplexer #(.width(32)) multiplexer_10 (
    .in0(cp0_1_dout), .in1(multiplexer_11_out), .out(multiplexer_10_out), .sel(not_3_out));
  not not_3 (not_3_out, IsCOP0);
  Multiplexer #(.width(32)) multiplexer_11 (
    .in0(adder_2_out), .in1(multiplexer_19_out), .out(multiplexer_11_out), .sel(not_4_out));
  not not_4 (not_4_out, IsJAL);
  Multiplexer multiplexer_12 (.in0(RegWrite), .in1(ExRegWrite), .out(multiplexer_12_out), .sel(undriven));
  Syscall_Decoder_7b4aca82 syscall_decoder_7b4aca82_1 (
    .v0(regfile_1_r1), .a0(regfile_1_r2), .clk(clk), .Enable(IsSyscall),
    .Hex({syscall_decoder_7b4aca82_1_hex_5, syscall_decoder_7b4aca82_1_hex_4, syscall_decoder_7b4aca82_1_hex_3, syscall_decoder_7b4aca82_1_hex_2, syscall_decoder_7b4aca82_1_hex}),
    .Halt(Halt));
  Multiplexer #(.width(32)) multiplexer_13 (
    .in0(regfile_1_r2), .in1(immediate_extender_0b85654b_1_output), .out(multiplexer_13_out), .sel(ALUSrc));
  assign bit_extender_1_out = {{27{multiplexer_5_out_2[12]}}, multiplexer_5_out_2[12:8]};  // Bit_Extender bit_extender_1
  Shifter #(.width(32)) shifter_1 (.in(immediate_extender_0b85654b_1_output), .\dist (5'b00010), .out(shifter_1_out));
  xor xor_1 (xor_1_out, Equal, BneOrBeq);
  Multiplexer #(.width(32)) multiplexer_14 (
    .in0(regfile_1_r1), .in1(regfile_1_r2), .out(multiplexer_14_out), .sel(IsShamt));
  Multiplexer #(.width(32)) multiplexer_15 (
    .in0(multiplexer_13_out), .in1(bit_extender_1_out), .out(multiplexer_15_out), .sel(IsShamt));
  Adder #(.width(32)) adder_3 (
    .a({multiplexer_5_out_2[31:28], adder_1_out}), .b(shifter_1_out), .out(adder_3_out));  // open: cin, cout
  Hex_Digit_Display hex_digit_display_1 (.value(syscall_decoder_7b4aca82_1_hex_5));  // open: dp
  Hex_Digit_Display hex_digit_display_2 (.value(syscall_decoder_7b4aca82_1_hex_4));  // open: dp
  // ALU alu_1: pin names not known; wires that end beside it: multiplexer_14_out, multiplexer_15_out, Equal, ALUop, alu_1_p5
  and and_2 (and_2_out, Branch, xor_1_out);
  Hex_Digit_Display hex_digit_display_3 (.value(syscall_decoder_7b4aca82_1_hex_3));  // open: dp
  Hex_Digit_Display hex_digit_display_4 (.value(syscall_decoder_7b4aca82_1_hex_2));  // open: dp
  Button button_1 (.out(ExpSrc0));
  Multiplexer #(.width(32)) multiplexer_16 (
    .in0({multiplexer_5_out_2[31:28], adder_1_out}), .in1(adder_3_out), .out(multiplexer_16_out),
    .sel(and_2_out));
  not not_5 (not_5_out, Jump);
  Hex_Digit_Display hex_digit_display_5 (.value(syscall_decoder_7b4aca82_1_hex[15:12]));  // open: dp
  Hex_Digit_Display hex_digit_display_6 (.value(syscall_decoder_7b4aca82_1_hex[11:8]));  // open: dp
  Button button_2 (.out(ExpSrc1));
  Multiplexer #(.width(32)) multiplexer_17 (
    .in0({multiplexer_5_out_2, 2'b00}), .in1(multiplexer_16_out), .out(multiplexer_17_out), .sel(not_5_out));
  Hex_Digit_Display hex_digit_display_7 (.value(syscall_decoder_7b4aca82_1_hex[7:4]));  // open: dp
  Hex_Digit_Display hex_digit_display_8 (.value(syscall_decoder_7b4aca82_1_hex[3:0]));  // open: dp
  interceptadorDeVideo interceptadordevideo_1 (
    .Write_Enable(MemWrite), .Adress_in(alu_1_p5[11:2]), .Data_in(regfile_1_r2),
    .Adress_out(interceptadordevideo_1_adress_out), .Data_out(interceptadordevideo_1_data_out),
    .Write_memory(interceptadordevideo_1_write_memory), .enable_video(interceptadordevideo_1_enable_video));  // open: in_4
  Button button_3 (.out(ExpSrc2));
  Multiplexer #(.width(32)) multiplexer_18 (
    .in0(multiplexer_17_out), .in1(regfile_1_r1), .out(multiplexer_18_out), .sel(IsJR));
  RAM #(.addrWidth(10), .dataWidth(32)) ram_1 (
    .addr(interceptadordevideo_1_adress_out), .we(interceptadordevideo_1_write_memory), .oe(MemRead),
    .clk(clk), .din(interceptadordevideo_1_data_out), .dout(ram_1_dout));
  controladorDisplay controladordisplay_1 (
    .data(interceptadordevideo_1_data_out), .clock(clk), .enable(interceptadordevideo_1_enable_video),
    .clear(clear_video), .address(interceptadordevideo_1_adress_out), .data_out(out_7), .X(out_4), .y(out_5),
    .color(out_6));
  Multiplexer #(.width(32)) multiplexer_19 (.in0(alu_1_p5), .in1(ram_1_dout), .out(multiplexer_19_out), .sel(MemtoReg));

  // Notes on the sheet:
  //   contents of rom_1 (hex, n*v repeats v):
  //   8c010004 8c210004 11042 ac220004 8c010004 8c010004 8c010004 8c210004 11042 ac220004 8c010004
  //   8c010004 8c010004 8c210004 11042 ac220004 8c010004 8c010004 8c010004 8c210004 11042 ac220004
  //   8c010004 8c010004 8c010004 8c210004 11042 ac220004 8c010004 8c010004 8c010004 8c210004 11042
  //   ac220004 8c010004 8c010004 8c010004 8c210004 11042 ac220004 8c010004 8c010004 8c010004 8c210004
  //   11042 ac220004 8c010004 8c010004 8c010004 8c210004 11042 ac220004 8c010004 8c010004 8c010004
  //   8c210004 11042 ac220004 8c010004 8c010004 8c010004 8c210004 11042 ac220004 8c010004 8c010004
  //   8c010004 8c210004 11042 ac220004 8c010004 8c010004 8c010004 8c210004 11042 ac220004 8c010004
  //   8c010004 8c010004 8c210004 11042 ac220004 8c010004 8c010004 8c010004 8c210004 11042 ac220004
  //   8c010004 8c010004 8c010004 8c210004 11042 ac220004 8c010004 8c010004 8c010004 8c210004 11042
  //   ac220004 8c010004 8c010004 8c010004 8c210004 11042 ac220004 8c010004 8c010004 8c010004 8c210004
  //   11042 ac220004 8c010004 8c010004 8c010004 8c210004 11042 ac220004 8c010004 8c010004 8c010004
  //   8c210004 11042 ac220004 8c010004 8c010004 8c010004 8c210004 11042 ac220004 8c010004 8c010004
  //   8c010004 8c210004 11042 ac220004 8c010004 8c010004 8c010004 8c210004 11042 ac220004 8c010004
  //   8c010004 8c010004 8c210004 11042 ac220004 8c010004 8c010004 8c010004 8c210004 11042 ac220004
  //   8c010004 8c010004 8c010004 8c210004 11042 ac220004 8c010004 8c010004
  //   Screen
endmodule

module Immediate_Extender_0b85654b (
  input  ZeroExtend,
  input  [15:0] Input,
  output [31:0] Output
);

  wire [31:0] bit_extender_1_out, bit_extender_2_out;

  assign bit_extender_1_out = {{16{Input[15]}}, Input};  // Bit_Extender bit_extender_1
  assign bit_extender_2_out = {{16{Input[15]}}, Input};  // Bit_Extender bit_extender_2
  Multiplexer #(.width(32)) multiplexer_1 (
    .in0(bit_extender_1_out), .in1(bit_extender_2_out), .out(Output), .sel(ZeroExtend));
endmodule
